# Fritzing sketch Untitled Sketch (saved by Fritzing 0.9.3b)
breadboards: 1
perfboards: 1

parts:
  元件1 = Arduino Motor Shield (Rev3)
  元件2 = Arduino Motor Shield (Rev3)
  元件3 = Arduino Mega ADK (Rev3)
  J1 = Infrared Proximity Sensor
  M1 = DC Motor
  M2 = DC Motor
  M3 = DC Motor
  M4 = DC Motor
  Power_plug1 = Power plug
  S1 = Pololu QTR-8 Reflectabce Sensor array [package=THT]
  S2 = Pololu QTR-8 Reflectabce Sensor array [package=THT]
  S3 = Pololu QTR-8 Reflectabce Sensor array [package=THT]
  S4 = Pololu QTR-8 Reflectabce Sensor array [package=THT]
  J2 = Infrared Proximity Sensor
  J3 = Infrared Proximity Sensor
  J4 = Infrared Proximity Sensor
  元件4 = InvenSense MPU6050
  S5 = Momentary Switch [package=ksa_sealed_tac_switch]
  R1 = Resistor [tolerance=±5% resistance=220 package="2010 [SMD]"]
  Btn1 = Adafruit Push-button Power Switch Breakout [package=THT]  # not connected

nets:
  N1: 元件1.A0, 元件2.A0, 元件3.A0
  N2: 元件1.A1, 元件2.A1, 元件3.A1
  N3: 元件1.A2, 元件2.A2, 元件3.A2
  N4: 元件1.A3, 元件2.A3, 元件3.A3
  N5: 元件1.A4, 元件2.A4, 元件3.A4
  N6: 元件1.A5, 元件2.A5, 元件3.A5
  N7: 元件1.D8/BreakeB, 元件2.D8/BreakeB, 元件3.D8_PWM
  N8: 元件1.D9/BreakeA, 元件2.D9/BreakeA, 元件3.D9_PWM
  N9: 元件1.D10_PWM, 元件2.D10_PWM, 元件3.D10_PWM
  N10: 元件1.D11_PWM/B, 元件2.D11_PWM/B, 元件3.D11_PWM
  N11: 元件1.D12/DirA, 元件2.D12/DirA, 元件3.D12_PWM
  N12: 元件1.D13/DirB, 元件2.D13/DirB, 元件3.D13_PWM
  GND: 元件1.GND, 元件2.GND, 元件3.GND, 元件3.D24, 元件3.D31, 元件3.D49, J1.GND, Power_plug1.GND, S1.pin1, S1.pin15, S1.pin16, S1.pin21, S2.pin15, S2.pin21, S3.pin15, S3.pin21, S4.pin15, S4.pin21, J2.GND, J3.GND, J4.GND, 元件4.GND, R1.Pin_1
  N13: 元件1.AREF, 元件2.AREF, 元件3.AREF
  N14: 元件1.IOREF#118, 元件2.IOREF#118, 元件3.D0/RX0
  N15: 元件1.D1/TX, 元件2.D1/TX, 元件3.D1/TX0
  N16: 元件1.D2, 元件2.D2, 元件3.D2_PWM
  N17: 元件1.D3_PWM/A, 元件2.D3_PWM/A, 元件3.D3_PWM
  N18: 元件1.D4, 元件2.D4, 元件3.D4_PWM
  N19: 元件1.D5_PWM, 元件2.D5_PWM, 元件3.D5_PWM
  N20: 元件1.D6_PWM, 元件2.D6_PWM, 元件3.D6_PWM
  N21: 元件1.D7, 元件2.D7, 元件3.D7_PWM
  N22: 元件1.B-, M1.pin_2
  N23: 元件1.B+, M1.pin_1
  N24: 元件1.A-, M2.pin_2
  N25: 元件1.VMOT, Power_plug1.VCC
  5V: 元件1.IOREF#147, 元件1.5V, 元件2.IOREF#147, 元件2.5V, 元件3.IOREF, 元件3.5V, 元件3.D23, 元件3.D30, 元件3.D48, S1.pin2, S1.pin14, S1.pin22, S2.pin14, S3.pin14, S3.pin22, S4.pin2, S4.pin14, S4.pin22, S5.4
  N26: 元件1.RESET, 元件2.RESET, 元件3.RESET
  VCC: 元件1.3V3, 元件2.3V3, 元件3.3V3, J1.Vcc, J2.Vcc, J3.Vcc, J4.Vcc, 元件4.VCC
  VIN: 元件1.VIN, 元件2.VIN, 元件3.VIN
  N27: 元件2.SDA, 元件3.D20/SDA, 元件4.SDA
  N28: 元件2.SCL, 元件3.D21/SCL, 元件4.SCL
  N29: 元件2.B-, M3.pin_2
  N30: 元件2.B+, M3.pin_1
  N31: 元件2.A-, M4.pin_2
  N32: 元件2.A+, M4.pin_1
  N33: 元件3.A8, J1.Vout
  N34: 元件3.A9, J2.Vout
  N35: 元件3.A10, J3.Vout
  N36: 元件3.A11, J4.Vout
  N37: 元件3.D14/TX3, S5.1
  N38: 元件3.D22, S1.pin23
  N39: 元件3.D25, S2.pin12
  N40: 元件3.D26, S2.pin11
  N41: 元件3.D27, S2.pin10
  N42: 元件3.D28, S2.pin9
  N43: 元件3.D29, S3.pin13, S3.pin23
  N44: 元件3.D47, S4.pin13, S4.pin23
  N45: S5.2, R1.Pin_0

notes:
  The size-5 reflectance sensor array at the back. Uses only 1st,3rd and 5th sensors.
  The size-5 reflectance sensor array at the front left. Uses only 1st,3rd and 5th sensors.
  The size-5 reflectance sensor array at the front right. Uses only 1st,3rd and 5th sensors.
  The size-9 reflectance sensor array at the front middle. Uses only 2nd,4th,6th and 8th sensors.
  Four distance sensors, uses analog pins A8~A11.
